# Fritzing sketch DHT22Wifi (saved by Fritzing 0.9.0b)
breadboards: 1

parts:
  Power_Regulator_Module = Voltage Regulator AMS1117 [package=sot223]
  part = ESP8266 WiFi Module [part_number=ESP8266]
  Power_Source = DC Power [voltage=5V]
  part_2 = Resistor [tolerance=±5% resistance=10k package=THT]
  AM1 = AM2302 Humidity and Temperature Sensor

nets:
  GND: Power_Regulator_Module.GND, part.GND, Power_Source.V-, AM1.GND
  VCC: Power_Regulator_Module.OUT, part.VCC, part_2.Pin_0, AM1.VDD
  N1: Power_Regulator_Module.IN, Power_Source.V+
  N2: part.GPIO_2, AM1.DATA
  N3: part.CH_PD, part_2.Pin_1

custom parts:
  ESP8266 WiFi Module: Generic WiFi Module based on the ESP8266 with onboard PCB antenna and UART communications
